# Fritzing sketch ChristouTempSense (saved by Fritzing 0.9.2b)
breadboards: 2

parts:
  LCD1 = LCD screen
  R2 = Resistor [tolerance=±5% resistance=56 package=THT]
  U1 = NodeMCU V1.0
  S1 = Momentary Switch [package=ksa_sealed_tac_switch]
  S2 = Momentary Switch [package=ksa_sealed_tac_switch]
  S3 = Momentary Switch [package=ksa_sealed_tac_switch]
  R3 = Temperature Sensor (Thermistor) [thermistor_type=NTC package=THT]
  R4 = Resistor [tolerance=±5% resistance=10k package=THT]
  U2 = 2-Channel 5v Relay Shield [package=relay-2ch5v10a]
  R5 = Resistor [tolerance=±5% resistance=4.6k package=THT]

nets:
  N1: LCD1.VSS, LCD1.R/W, LCD1.LED-, U2.JD-GND, R5.Pin_0
  N2: LCD1.VDD, R2.Pin_1, U2.JD-VCC
  N3: LCD1.V0, R5.Pin_1
  N4: LCD1.RS, U1.D1
  N5: LCD1.E, U1.D2
  N6: LCD1.DB4, U1.D3
  N7: LCD1.DB5, U1.D4
  N8: LCD1.DB6, U1.RX
  N9: LCD1.DB7, U1.SD3
  N10: LCD1.LED+, R2.Pin_0
  N11: U1.D0, U2.IN1, U2.IN2
  3V3: U1.3V3, R3.pin_0, U2.VCC
  N12: U1.GND, S1.1, S2.1, S3.1, R4.Pin_1
  N13: U1.D5, S1.4
  N14: U1.D6, S2.4
  N15: U1.D7, S3.4
  N16: U1.A0, R3.pin_1, R4.Pin_0

notes:
  Direct 5v power here
  (ie. via USB connector)
  2 channel relay module JD-VCC connector isn't showing up properly in Fritzing. The JD-VCC connects to the Direct 5v power rail. VCC (the one beside JD-VCC) connects to 3v3 power from NodeMCU/ESP8266.
  NOTE: Only Breadboard view of Fritzing diagram is useable. All other views should not be used.
  TO 240VAC FAN
  Both relays are used to switch both the Active/Live and Neutral wires of the mains power.
  Earth wire remains untouched.
  To fan Active/Live wire
  To main power Active/Live wire
  To fan Neutral wire
  To main powerNeutral wire

custom parts:
  NodeMCU V1.0: ESP8266 based NodeMCU
  2-Channel 5v Relay Shield: 2 Channel 5v Relay Shield w. 2x SPD-06VDC-SD-C
